# Fritzing sketch ServoTester_I2C (saved by Fritzing 0.9.9b)
breadboards: 1

parts:
  Part1 = Arduino Nano (Rev3.0)
  U1 = Voltage Regulator - 5V [package="TO220 [THT]"]
  Part2 = LCD1602-I2C
  J1 = Basic Servo
  S1 = Pushbutton [part_number=Mode package="[THT]"]
  S2 = Pushbutton [part_number=Minus package="[THT]"]
  S3 = Pushbutton [part_number=Plus package="[THT]"]
  Power_plug1 = Power plug [part_number=12VDC]

nets:
  VIN: Part1.VIN, U1.input_voltage, Power_plug1.VCC
  GND: Part1.GND, U1.GND, S1.Pin_1, S1.Pin_2, Power_plug1.GND
  N1: Part1.A5, Part2.SCL
  N2: Part1.A4, Part2.SDA
  N3: Part1.A3, S3.Pin_3
  N4: Part1.A2, S2.Pin_3, S2.Pin_4
  N5: Part1.A1, S1.Pin_3
  N6: Part1.A0, J1.pulse
  VCC: U1.output_voltage, Part2.VCC, J1.vcc
  GND_2: Part2.GND, J1.gnd

custom parts:
  LCD1602-I2C: A standard character display, usually with 2x16 characters. Comes in many colors with LCM1602 IIC attached.
